# Fritzing sketch fritzing_layout (saved by Fritzing 0.9.3b)

parts:
  Teensy1 = Teensy 4.0
  S2 = SWITCH-MOMENTARY-2 [package=tactile-switch-1101ne]
  S3 = SWITCH-MOMENTARY-2 [package=tactile-switch-1101ne]
  S4 = SWITCH-MOMENTARY-2 [package=tactile-switch-1101ne]
  S5 = SWITCH-MOMENTARY-2 [package=tactile-switch-1101ne]
  S6 = SWITCH-MOMENTARY-2 [package=tactile-switch-1101ne]
  S7 = SWITCH-MOMENTARY-2 [package=tactile-switch-1101ne]
  LED1 = smd LED [color="Red (633nm)" package="1206 [SMD]"]
  LED2 = smd LED [color="Red (633nm)" package="1206 [SMD]"]
  LED3 = smd LED [color="Red (633nm)" package="1206 [SMD]"]
  LED4 = smd LED [color="Red (633nm)" package="1206 [SMD]"]
  LED5 = smd LED [color="Red (633nm)" package="1206 [SMD]"]
  LED6 = smd LED [color="Red (633nm)" package="1206 [SMD]"]
  J1 = Camdenboss CTB0158-6 [part_number=CTB0158-6 package=THT]
  J2 = Camdenboss CTB0158-6 [part_number=CTB0158-6 package=THT]

nets:
  N1: Teensy1.pin_1, J1.pin1, J1.pin2, J1.pin3, J1.pin4, J1.pin5, J1.pin6, J2.pin1, J2.pin2, J2.pin3, J2.pin4, J2.pin5, J2.pin6
  N2: Teensy1.pin_4, S7.1
  N3: Teensy1.pin_5, S6.1
  N4: Teensy1.pin_6, S5.1
  N5: Teensy1.pin_7, S4.1
  N6: Teensy1.pin_9, S3.1
  N7: Teensy1.pin_11, S2.1
  N8: Teensy1.pin_24, LED2.anode
  N9: Teensy1.pin_25, LED3.anode
  N10: Teensy1.pin_26, LED4.anode
  N11: Teensy1.pin_27, LED5.anode
  N12: Teensy1.pin_28, LED1.anode
  N13: Teensy1.pin_29, LED6.anode
  N14: S2.2, J2.terminal_6
  N15: S3.2, J2.terminal_5
  N16: S4.2, J2.terminal_4
  N17: S5.2, J2.terminal_3
  N18: S6.2, J2.terminal_2
  N19: S7.2, J2.terminal_1
  N20: LED1.cathode, J1.terminal_2
  N21: LED2.cathode, J1.terminal_6
  N22: LED3.cathode, J1.terminal_5
  N23: LED4.cathode, J1.terminal_4
  N24: LED5.cathode, J1.terminal_3
  N25: LED6.cathode, J1.terminal_1

custom parts:
  Teensy 4.0: The Teensy is a complete USB-based microcontoller development system, in a very small footprint, capable of implementing many types of projects. All programming is done via the USB port. No special programmer is needed, only a standard micro-USB cable and a PC or Macintosh with a USB port.
